# Fritzing sketch IR_Obstacle (saved by Fritzing 0.9.4)
breadboards: 1

parts:
  Part1 = Arduino Uno (Rev3)
  HC-SR04_Sensor_1 = HC-SR04 Ultrasonic Distance Sensor
  Part2 = OLED Monochrome 128x64 0.96 inch [part_number=326]  # not connected

nets:
  N1: Part1.D6_PWM, HC-SR04_Sensor_1.TRIG
  N2: Part1.D7, HC-SR04_Sensor_1.ECHO
  5V: Part1.5V, HC-SR04_Sensor_1.VCC
  GND: Part1.GND, HC-SR04_Sensor_1.GND

custom parts:
  OLED Monochrome 128x64 0.96 inch: These displays are small, only about 1" diameter, but very readable due to the high contrast of an OLED display. This display is made of 128x64 individual white OLED pixels, each one is turned on or off by the controller chip. Because the display makes its own light, no backlight is required. This reduces the power required to run the OLED and is why the display has such high contrast; we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
