# Fritzing sketch IR_Servo (saved by Fritzing 0.9.4)
breadboards: 1

parts:
  Part1 = Arduino Uno (Rev3)
  Part2 = KY-012 Active Buzzer Module [package="Breakout board"]
  IR1 = TSOP312.., 314.. [package=THT]
  LED1 = RGB LED (com. cathode, rgb) [package="5 mm [THT]"]

nets:
  N1: Part1.D9_PWM, IR1.Data
  N2: Part1.D2, Part2.S
  N3: Part1.D3_PWM, LED1.blue_anode
  N4: Part1.D5_PWM, LED1.green_anode
  N5: Part1.D6_PWM, LED1.red_anode
  N6: Part1.5V, IR1.Vs
  GND: Part1.GND, Part2.-, IR1.GND, LED1.common_cathode

custom parts:
  KY-012 Active Buzzer Module: Active Piezoelectric Buzzer Module Keyes KY-012, it produces single-tone sound when signal is high.
