# Fritzing sketch OLED_basic (saved by Fritzing 0.9.4)
breadboards: 1

parts:
  Part1 = Arduino Uno (Rev3)
  Part3 = OLED Monochrome 128x64 0.96 inch [part_number=326]

nets:
  N1: Part1.D9_PWM, Part3.MOSI_SDA
  N2: Part1.D10_PWM/SS, Part3.SCLK_SCK
  N3: Part1.D11_PWM/MOSI, Part3.DC_SA0
  N4: Part1.D12/MISO, Part3.CS
  N5: Part1.D13/SCK, Part3.RESET
  5V: Part1.5V, Part3.VIN
  GND: Part1.GND, Part3.GND

custom parts:
  OLED Monochrome 128x64 0.96 inch: These displays are small, only about 1" diameter, but very readable due to the high contrast of an OLED display. This display is made of 128x64 individual white OLED pixels, each one is turned on or off by the controller chip. Because the display makes its own light, no backlight is required. This reduces the power required to run the OLED and is why the display has such high contrast; we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
