# Fritzing sketch ds18b20 (saved by Fritzing 0.9.4)
breadboards: 1

parts:
  DS1 = DS18B20 1-Wire Temperature Sensor [part_number=DS18B20]
  Part3 = Arduino Nano (Rev3.0)
  R1 = Resistor [tolerance=±5% resistance=5k package="2010 [SMD]"]

nets:
  GND: DS1.GND, Part3.GND
  N1: DS1.DQ, Part3.A1, R1.Pin_1
  VDD: DS1.VDD, Part3.5V, R1.Pin_0
